# Fritzing sketch air-quality (saved by Fritzing 1.0.2b)
breadboards: 1

parts:
  Part1 = Arduino Uno (Rev3)
  U1 = ESP8266 WiFi Module [part_number=ESP8266]
  R4 = Resistor [tolerance=±5% power=0.25W resistance=1k package=THT]
  R5 = Resistor [tolerance=±5% power=0.25W resistance=1k package=THT]
  R6 = Resistor [tolerance=±5% power=0.25W resistance=10k package=THT]

nets:
  N1: Part1.D0/RX, R4.Pin_0
  N2: Part1.RESET, U1.RST
  3V3: Part1.3V3, U1.VCC, U1.CH_PD, R6.Pin_0, R6.Pin_1
  GND: Part1.GND, U1.GND, R5.Pin_1
  N3: U1.RXD, R4.Pin_1, R5.Pin_0

custom parts:
  ESP8266 WiFi Module: Generic WiFi Module based on the ESP8266 with onboard PCB antenna and UART communications
